# Fritzing sketch MQTT-keypad v2.5 (produida) (saved by Fritzing 0.9.3b)
circuit board: 7.6cm x 7.6cm
breadboards: 1

parts:
  AC220/DV12 = screw terminal, 2 pins
  HLK-PM1 = HLK-PM01
  J3 = female pin header, 8 pins [form="♀ (female)"]
  J4 = female pin header, 4 pins [form="♀ (female)"]
  J5 = female pin header, 2 pins [form="♀ (female)"]
  J7 = male pin header, 4 pins [form="♂ (male)"]
  J8 = female pin header, 1 pin [form="♀ (female)"]
  DC-Power = male pin header, 2 pins [form="♂ (male)"]
  J9 = male pin header, 9 pins [form="♂ (male)"]
  D3 = male pin header, 3 pins [form="♂ (male)"]
  MAX485 = MAX485 [package=dil08]
  -LED+ = male pin header, 2 pins [form="♂ (male)"]
  U1 = Voltage Regulator - 5V [package="TO220 [THT]"]
  C3 = Electrolytic Capacitor [capacitance=470µF package="200 mil [THT, electrolytic]"]
  D7 = Rectifier Diode [part_number=1N4001 package="300 mil [THT]"]
  J11 = female pin header, 2 pins [form="♀ (female)"]
  R1 = Resistor [tolerance=±20% resistance=330 package=THT]
  PCF8574P = PCF8574 [package="DIP16 [THT]"]
  AC1 = screw terminal, 6 pins
  R3 = Resistor [tolerance=±5% resistance=10k package=THT]
  R4 = Resistor [tolerance=±5% resistance=10k package=THT]
  D5/TX = male pin header, 3 pins [form="♂ (male)"]
  W = WeMos D1 Mini
  GRN = female pin header, 1 pin [form="♀ (female)"]
  C1 = Electrolytic Capacitor [capacitance=1µF voltage=0.1kV package="200 mil [THT, electrolytic]"]
  Fuse = Resettable Fuse PTC [package=ptc]
  AC-Power = male pin header, 2 pins [form="♂ (male)"]

nets:
  N1: AC220/DV12.pin1, AC-Power.pin2
  N2: AC220/DV12.pin2, HLK-PM1.AC#0, J11.pin2
  N3: HLK-PM1.AC#1, D7.anode, Fuse.1
  N4: HLK-PM1.-Vo, J7.pin1, DC-Power.pin1, U1.GND, C3.-, J11.pin1, C1.-
  VCC: HLK-PM1.+Vo, MAX485.VCC, U1.output_voltage, AC1.pin6, W.5V, C1.+
  N5: J3.pin1, PCF8574P.P0
  N6: J3.pin2, PCF8574P.P1
  N7: J3.pin3, PCF8574P.P2
  N8: J3.pin4, PCF8574P.P3
  N9: J3.pin5, PCF8574P.P4
  N10: J3.pin6, PCF8574P.P5
  N11: J3.pin7, J3.pin8, PCF8574P.P6, PCF8574P.P7
  GND: J4.pin1, J5.pin1, DC-Power.pin2, J9.pin1, D3.pin3, MAX485.RE, MAX485.DE, MAX485.GND, -LED+.pin2, PCF8574P.A0, PCF8574P.A1, PCF8574P.A2, PCF8574P.GND, AC1.pin5, W.G, GRN.pin1
  VCC_2: J4.pin2, J9.pin9, PCF8574P.VCC, R3.Pin_1, R4.Pin_1, W.3V3
  N12: J4.pin3, PCF8574P.SCL, R3.Pin_0, W.D1
  N13: J4.pin4, PCF8574P.SDA, R4.Pin_0, W.D2
  N14: J5.pin2, J9.pin6, R1.Pin_0, W.D6
  N15: J7.pin4, J9.pin7, W.D7
  N16: J8.pin1, PCF8574P.INT
  N17: J9.pin2, W.RST
  N18: J9.pin3, W.A0
  N19: J9.pin4, W.D0
  N20: J9.pin5, D5/TX.pin3, W.D5
  N21: J9.pin8, W.D8
  N22: D3.pin1, W.D3
  N23: D3.pin2, W.D4
  N24: MAX485.RO, D5/TX.pin2
  N25: MAX485.DI, AC1.pin2, W.TX
  N26: MAX485.A, AC1.pin3
  N27: MAX485.B, AC1.pin4
  N28: -LED+.pin1, R1.Pin_1
  N29: U1.input_voltage, C3.+, D7.cathode
  N30: AC1.pin1, D5/TX.pin1, W.RX
  N31: Fuse.2, AC-Power.pin1

notes:
  buzzer D7
  D0
  D7
  +
  DomIoT
  3V3
  GND
  RST
  A0
  D8
  D5
  D6
  D4
  MQTT-KeyPad
  v2.1
  -
  RXTX A+ B+GR+5v
  LM7805
